# Fritzing sketch lipocutoff (saved by Fritzing 0.8.3b)
circuit board: 4.2cm x 3.2cm
breadboards: 1

parts:
  U1 = attiny85 [package=dip]
  BAT1 = Battery Holders [package=battcon_12mm]
  Q1 = Basic FET N-Channel [package="TO220 [THT]"]  # not connected
  Pad1 = Pad [width=7.90222222222222 height=9.03111111111111 connect=center]  # not connected
  Pad2 = Pad [width=7.90222222222222 height=9.03111111111111 connect=center]  # not connected
  Pad3 = Pad [width=7.90222222222222 height=9.03111111111111 connect=center]  # not connected
  Pad4 = Pad [width=7.90222222222222 height=9.03111111111111 connect=center]  # not connected

nets:
  N1: U1.Pin_4, BAT1.-
  N2: U1.Pin_8, BAT1.+
